// Logisim project HEHE.circ as structural Verilog: 1 circuit, main circuit main
module main (
  input  C1,
  input  C0,
  output Y
);

  wire CLK_out, d_ff_1_q, d_ff_2_q, nand_1_out, nand_2_out, nand_3_out, nand_4_out, nand_5_out, nand_6_out,
       nand_7_out, nand_8_out, nand_9_out, nand_10_out, not_1_out, not_2_out, not_3_out, not_4_out, Reset_out;

  not not_1 (not_1_out, C1);
  not not_2 (not_2_out, C0);
  not not_3 (not_3_out, d_ff_1_q);
  not not_4 (not_4_out, d_ff_2_q);
  nand nand_1 (nand_1_out, C1, not_2_out, not_3_out);
  nand nand_2 (nand_2_out, not_1_out, C0, not_3_out, d_ff_2_q);
  nand nand_3 (nand_3_out, d_ff_1_q, not_4_out);
  nand nand_4 (nand_4_out, not_1_out, C0, not_4_out);
  nand nand_5 (nand_5_out, not_2_out, not_3_out, d_ff_2_q);
  nand nand_6 (nand_6_out, C1, not_3_out, d_ff_2_q);
  nand nand_7 (nand_7_out, C1, not_2_out, d_ff_1_q, not_4_out);
  Clock CLK (.out(CLK_out));
  nand nand_8 (nand_8_out, nand_1_out, nand_2_out, nand_3_out);
  nand nand_9 (nand_9_out, nand_4_out, nand_5_out, nand_6_out, nand_7_out);
  D_Flip_Flop d_ff_1 (.clk(CLK_out), .D(nand_8_out), .Q(d_ff_1_q), .reset(Reset_out));  // open: Qn, preset, en
  D_Flip_Flop d_ff_2 (.clk(CLK_out), .D(nand_9_out), .Q(d_ff_2_q), .reset(Reset_out));  // open: Qn, preset, en
  nand nand_10 (nand_10_out, d_ff_1_q, d_ff_2_q);
  Button Reset (.out(Reset_out));
  not not_5 (Y, nand_10_out);

  // Notes on the sheet:
  //   S1
  //   S0
  //   S1'
  //   S0'
  //   S1
  //   S0
endmodule
